// Logisim project Cache.circ as structural Verilog: 10 circuits, main circuit main
module main (
  input  [15:0] in_1,
  input  in_2,
  input  [15:0] in_3,
  input  in_4,
  input  in_5,
  input  in_6,
  output [9:0] out_7
);

  wire CacheToReg, clock, IsBranch, j_k_ff_2_q, Jump, not_1_out, not_2_out, not_3_out, not_4_out, not_5_out,
       not_6_out, not_7_out, not_8_out, not_9_out, not_10_out, not_11_out, not_12_out, not_13_out,
       not_14_out, not_19_out, not_20_out, not_21_out, not_22_out, not_24_out, not_25_out, pcAtualizou,
       processador_1_out_10, stall, stall2, store;
  wire [9:0] adder_1_out, addressPC, Desloc, JumpAddress, multiplexer_1_out, multiplexer_2_out,
       multiplexer_3_out, multiplexer_5_out, multiplexer_6_out, not_15_out, not_16_out, not_17_out,
       not_18_out, not_26_out, not_27_out, not_28_out, not_29_out, not_30_out, not_31_out, not_32_out,
       not_33_out, not_34_out, not_36_out, not_37_out, processador_1_readaddress, ReadAddress;
  wire [9:1] multiplexer_4_out;
  wire [15:0] data, Instruction, Instruction1, Instruction2, Instruction3, Instruction4, outputmp;

  Clock clock_1 (.out(clock));
  Multiplexer #(.width(10), .enable("false")) multiplexer_1 (
    .in0(addressPC), .in1(ReadAddress), .out(multiplexer_1_out), .sel(CacheToReg));
  J_K_Flip_Flop j_k_ff_1 (.J(stall), .clk(clock), .K(not_1_out), .Q(store));  // open: Qn, preset, en, reset
  not not_1 (not_1_out, stall);
  or or_1 (stall2, stall, store);
  Multiplexer #(.width(10), .enable("false")) multiplexer_2 (
    .in0(multiplexer_6_out), .in1(10'h4), .out(multiplexer_2_out), .sel(in_6));
  Multiplexer #(.width(10), .enable("false")) multiplexer_3 (
    .in0(addressPC), .in1(ReadAddress), .out(multiplexer_3_out), .sel(CacheToReg));
  Multiplexer #(.width(10), .enable("false")) multiplexer_4 (
    .in0(10'h1), .in1({10{1'b0}}), .out({multiplexer_4_out, pcAtualizou}), .sel(stall2));
  Register #(.width(10)) PC (.D(multiplexer_2_out), .en(1'b1), .Q(addressPC), .clk(clock));  // open: clr
  MP Memoria_Principal (
    .inputData(in_1), .store(in_2), .address(multiplexer_1_out), .outputData(Instruction1),
    .outputData_2(Instruction2), .outputData_3(Instruction3), .outputData_4(Instruction4));
  Controle_cache ControleCache (.cacheStatus(stall), .store(store), .address(multiplexer_3_out));
  Adder #(.width(10)) adder_1 (
    .a({multiplexer_4_out, pcAtualizou}), .b(addressPC), .out(adder_1_out));  // open: cin, cout
  Multiplexer #(.width(10), .enable("false")) multiplexer_5 (
    .in0(adder_1_out), .in1(Desloc), .out(multiplexer_5_out), .sel(IsBranch));
  Multiplexer #(.width(10), .enable("false")) multiplexer_6 (
    .in0(JumpAddress), .in1(multiplexer_5_out), .out(multiplexer_6_out), .sel(not_2_out));
  not not_2 (not_2_out, Jump);
  Cache Memoria_Cache (
    .input1(Instruction1), .input2(Instruction2), .input3(Instruction3), .input4(Instruction4),
    .store(store), .out_9(Instruction), .address(addressPC), .address2(ReadAddress), .out_10(data),
    .CacheToReg(CacheToReg));
  not not_3 (not_3_out, pcAtualizou);
  J_K_Flip_Flop j_k_ff_2 (.J(pcAtualizou), .clk(clock), .K(not_3_out), .Q(j_k_ff_2_q));  // open: Qn, preset, en, reset
  not not_4 (not_4_out, processador_1_out_10);
  not not_5 (not_5_out, not_4_out);
  not not_6 (not_6_out, not_7_out);
  not not_7 (not_7_out, not_19_out);
  Processador processador_1 (
    .dado(data), .Instrucao(Instruction), .IsBranch(IsBranch), .Jump(Jump), .JumpAddress(JumpAddress),
    .readAddress(processador_1_readaddress), .out_10(processador_1_out_10), .in_1(stall2),
    .Deslocamento(Desloc), .in_3(j_k_ff_2_q));
  not not_8 (not_8_out, not_9_out);
  not not_9 (not_9_out, not_10_out);
  not not_10 (not_10_out, not_5_out);
  not not_11 (not_11_out, not_12_out);
  not not_12 (not_12_out, not_6_out);
  not not_13 (not_13_out, not_11_out);
  Multiplexer #(.select(2), .width(16), .enable("false")) multiplexer_7 (
    .in0(Instruction1), .in1(Instruction2), .in2(Instruction3), .in3(Instruction4), .out(outputmp),
    .sel(addressPC[1:0]));
  not not_14 (not_14_out, clock);
  assign not_15_out = ~processador_1_readaddress;  // NOT_Gate not_15, 10 bits wide
  assign not_16_out = ~not_15_out;  // NOT_Gate not_16, 10 bits wide
  assign not_17_out = ~not_18_out;  // NOT_Gate not_17, 10 bits wide
  assign not_18_out = ~not_32_out;  // NOT_Gate not_18, 10 bits wide
  not not_19 (not_19_out, not_20_out);
  not not_20 (not_20_out, not_21_out);
  not not_21 (not_21_out, not_8_out);
  not not_22 (not_22_out, not_13_out);
  not not_23 (CacheToReg, not_24_out);
  not not_24 (not_24_out, not_22_out);
  not not_25 (not_25_out, not_14_out);
  assign not_26_out = ~not_27_out;  // NOT_Gate not_26, 10 bits wide
  assign not_27_out = ~not_16_out;  // NOT_Gate not_27, 10 bits wide
  assign not_28_out = ~not_26_out;  // NOT_Gate not_28, 10 bits wide
  assign not_29_out = ~not_31_out;  // NOT_Gate not_29, 10 bits wide
  assign not_30_out = ~not_17_out;  // NOT_Gate not_30, 10 bits wide
  assign not_31_out = ~not_30_out;  // NOT_Gate not_31, 10 bits wide
  Register #(.width(10)) register_1 ();  // open: D, en, Q, clk, clr
  assign not_32_out = ~not_33_out;  // NOT_Gate not_32, 10 bits wide
  assign not_33_out = ~not_34_out;  // NOT_Gate not_33, 10 bits wide
  assign not_34_out = ~not_28_out;  // NOT_Gate not_34, 10 bits wide
  assign ReadAddress = ~not_36_out;  // NOT_Gate not_35, 10 bits wide
  assign not_36_out = ~not_37_out;  // NOT_Gate not_36, 10 bits wide
  assign not_37_out = ~not_29_out;  // NOT_Gate not_37, 10 bits wide

  // Other names for the same wires on the sheet: reset = in_6; row[2:0] = addressPC[4:2];
  //   row1[2:0] = ReadAddress[4:2]; tag[4:0] = addressPC[9:5]; tag1[4:0] = ReadAddress[9:5];
  //   word[1:0] = addressPC[1:0]; word1[1:0] = ReadAddress[1:0]

  // Notes on the sheet:
  //   PC
endmodule

module MP (
  input  [15:0] inputData,
  input  [9:0] address,
  input  store,
  output [15:0] outputData,
  output [15:0] outputData_2,
  output [15:0] outputData_3,
  output [15:0] outputData_4
);

  wire CLK, demultiplexer_1_out0, demultiplexer_1_out1, demultiplexer_1_out2, demultiplexer_1_out3,
       not_1_out, not_2_out, not_3_out, not_4_out;

  Clock clock_1 (.out(CLK));
  Demultiplexer #(.select(2), .enable("false")) demultiplexer_1 (
    .out0(demultiplexer_1_out0), .out1(demultiplexer_1_out1), .out2(demultiplexer_1_out2),
    .out3(demultiplexer_1_out3), .in(store), .sel(address[1:0]));
  assign outputData = demultiplexer_1_out0 ? inputData : 16'bz;  // Controlled_Buffer controlled_buffer_1
  assign outputData_2 = demultiplexer_1_out1 ? inputData : 16'bz;  // Controlled_Buffer controlled_buffer_2
  assign outputData_3 = demultiplexer_1_out2 ? inputData : 16'bz;  // Controlled_Buffer controlled_buffer_3
  assign outputData_4 = demultiplexer_1_out3 ? inputData : 16'bz;  // Controlled_Buffer controlled_buffer_4
  not not_1 (not_1_out, demultiplexer_1_out0);
  not not_2 (not_2_out, demultiplexer_1_out1);
  not not_3 (not_3_out, demultiplexer_1_out2);
  not not_4 (not_4_out, demultiplexer_1_out3);
  RAM #(.dataWidth(16)) ram_1 (.addr(address[9:2]), .data(outputData), .clk(CLK), .ld(not_1_out));  // open: sel, clr
  RAM #(.dataWidth(16)) ram_2 (.addr(address[9:2]), .data(outputData_2), .clk(CLK), .ld(not_2_out));  // open: sel, clr
  RAM #(.dataWidth(16)) ram_3 (.addr(address[9:2]), .data(outputData_3), .clk(CLK), .ld(not_3_out));  // open: sel, clr
  RAM #(.dataWidth(16)) ram_4 (.addr(address[9:2]), .data(outputData_4), .clk(CLK), .ld(not_4_out));  // open: sel, clr
endmodule

module Linha (
  input  [15:0] inputData1,
  input  [15:0] inputData2,
  input  store,
  input  [1:0] word,
  input  [15:0] inputData3,
  input  [15:0] inputData4,
  input  [1:0] word2,
  output [15:0] \output ,
  output [15:0] output2
);

  wire CLK;
  wire [15:0] output1, output2_t, output3, output4;

  Clock clock_1 (.out(CLK));
  Register #(.width(16)) register_1 (.D(inputData1), .en(store), .Q(output1), .clk(CLK));  // open: clr
  Register #(.width(16)) register_2 (.D(inputData2), .en(store), .Q(output2_t), .clk(CLK));  // open: clr
  Register #(.width(16)) register_3 (.D(inputData3), .en(store), .Q(output3), .clk(CLK));  // open: clr
  Register #(.width(16)) register_4 (.D(inputData4), .en(store), .Q(output4), .clk(CLK));  // open: clr
  Multiplexer #(.select(2), .width(16), .enable("false")) multiplexer_1 (
    .in0(output1), .in1(output2_t), .in2(output3), .in3(output4), .out(\output ), .sel(word));
  Multiplexer #(.select(2), .width(16), .enable("false")) multiplexer_2 (
    .in0(output1), .in1(output2_t), .in2(output3), .in3(output4), .out(output2), .sel(word2));
endmodule

module Cache (
  input  [15:0] input1,
  input  [15:0] input2,
  input  [15:0] input3,
  input  [15:0] input4,
  input  store,
  input  CacheToReg,
  input  [9:0] address,
  input  [9:0] address2,
  output [15:0] out_9,
  output [15:0] out_10
);

  wire row1, row2, row3, row4, row5, row6, row7, row8;
  wire [1:0] word;
  wire [2:0] row;
  wire [15:0] output1, output2, output3, output4, output5, output6, output7, output8, OutputData1,
       OutputData2, OutputData3, OutputData4, OutputData5, OutputData6, OutputData7, OutputData8;

  Demultiplexer #(.select(3), .enable("false")) demultiplexer_1 (
    .out0(row1), .out1(row2), .out2(row3), .out3(row4), .out4(row5), .out5(row6), .out6(row7), .out7(row8),
    .in(store), .sel(row));
  Multiplexer #(.width(3), .enable("false")) multiplexer_1 (
    .in0(address[4:2]), .in1(address2[4:2]), .out(row), .sel(CacheToReg));
  Multiplexer #(.width(2), .enable("false")) multiplexer_2 (
    .in0(address[1:0]), .in1(address2[1:0]), .out(word), .sel(CacheToReg));
  Linha linha_1 (
    .inputData1(input1), .inputData2(input2), .inputData3(input3), .store(row1), .word(word),
    .inputData4(input4), .\output (output1), .output2(OutputData1), .word2(address2[1:0]));
  Linha linha_2 (
    .inputData1(input1), .inputData2(input2), .inputData3(input3), .store(row2), .word(word),
    .inputData4(input4), .\output (output2), .output2(OutputData2), .word2(address2[1:0]));
  Linha linha_3 (
    .inputData1(input1), .inputData2(input2), .inputData3(input3), .store(row3), .word(word),
    .inputData4(input4), .\output (output3), .output2(OutputData3), .word2(address2[1:0]));
  Linha linha_4 (
    .inputData1(input1), .inputData2(input2), .inputData3(input3), .store(row4), .word(word),
    .inputData4(input4), .\output (output4), .output2(OutputData4), .word2(address2[1:0]));
  Linha linha_5 (
    .inputData1(input1), .inputData2(input2), .inputData3(input3), .store(row5), .word(word),
    .inputData4(input4), .\output (output5), .output2(OutputData5), .word2(address2[1:0]));
  Linha linha_6 (
    .inputData1(input1), .inputData2(input2), .inputData3(input3), .store(row6), .word(word),
    .inputData4(input4), .\output (output6), .output2(OutputData6), .word2(address2[1:0]));
  Linha linha_7 (
    .inputData1(input1), .inputData2(input2), .inputData3(input3), .store(row7), .word(word),
    .inputData4(input4), .\output (output7), .output2(OutputData6), .word2(address2[1:0]));
  Linha linha_8 (
    .inputData1(input1), .inputData2(input2), .inputData3(input3), .store(row8), .word(word),
    .inputData4(input4), .\output (output8), .output2(OutputData6), .word2(address2[1:0]));
  Multiplexer #(.select(3), .width(16), .enable("false")) multiplexer_3 (
    .in0(output1), .in1(output2), .in2(output3), .in3(output4), .in4(output5), .in5(output6), .in6(output7),
    .in7(output8), .out(out_9), .sel(address[4:2]));
  Multiplexer #(.select(3), .width(16), .enable("false")) multiplexer_4 (
    .in0(OutputData1), .in1(OutputData2), .in2(OutputData3), .in3(OutputData4), .in4(OutputData5),
    .in5(OutputData6), .in6(OutputData7), .in7(OutputData8), .out(out_10), .sel(address2[4:2]));

  // Other names for the same wires on the sheet: InstructionWord[1:0] = address[1:0];
  //   InstructionRow[2:0] = address[4:2]; dataWord[1:0] = address2[1:0]; dataRow[2:0] = address2[4:2];
  //   word1[15:0] = input1; word2[15:0] = input2; word3[15:0] = input3; word4[15:0] = input4
endmodule

// CC
module Controle_cache (
  input  store,
  input  [9:0] address,
  output cacheStatus
);

  wire CLK, comparator_1_eq, not_1_out;
  wire [5:0] bit_extender_1_out, controlled_buffer_1_out, Tag;

  Clock clock_1 (.out(CLK));
  assign controlled_buffer_1_out = store ? Tag : 6'bz;  // Controlled_Buffer controlled_buffer_1
  assign bit_extender_1_out = {{1{1'b0}}, address[9:5]};  // Bit_Extender bit_extender_1
  not not_1 (not_1_out, store);
  Adder #(.width(6)) adder_1 (.a(6'b000001), .b(bit_extender_1_out), .out(Tag));  // open: cin, cout
  RAM #(.addrWidth(3), .dataWidth(6)) ram_1 (
    .addr(address[4:2]), .data(controlled_buffer_1_out), .clk(CLK), .ld(not_1_out));  // open: sel, clr
  Comparator #(.width(6)) comparator_1 (.a(controlled_buffer_1_out), .b(Tag), .eq(comparator_1_eq));  // open: gt, lt
  not not_2 (cacheStatus, comparator_1_eq);

  // Other names for the same wires on the sheet: row[2:0] = address[4:2]

  // Notes on the sheet:
  //   Soma 1 a tag para ignorar a Tag 0
  //   Armazena a Tag
  //   CacheStatus:
  //   0 - Cache Hit
  //   1 - Cache Miss
endmodule

module Processador (
  input  in_1,
  input  [15:0] dado,
  input  in_3,
  input  [15:0] Instrucao,
  output [9:0] Deslocamento,
  output IsBranch,
  output Jump,
  output [9:0] JumpAddress,
  output [9:0] readAddress,
  output out_10
);

  wire AluSrc, Branch, CacheRead, CacheToReg, CacheWrite, Clock, IsBranch_t, RegDst, RegWrite, ula_1_igual;
  wire [1:0] controleula_1_controle;
  wire [2:0] ALUOP;
  wire [9:0] Desloc;
  wire [15:0] \banco_de_registradores_1_saída1 , \banco_de_registradores_1_saída2 , bit_extender_2_out,
       Dado_t, multiplexer_1_out;
  wire [15:10] \ula_1_saída ;

  Clock u_clock (.out(Clock));
  assign Desloc = {{3{1'b0}}, Instrucao[6:0]};  // Bit_Extender bit_extender_1
  Unidade_de_Controle unidade_de_controle_1 (
    .RegDst(RegDst), .RegWrite(RegWrite), .ALUSrc(AluSrc), .MemRead(CacheRead), .MemWrite(CacheWrite),
    .Branch(Branch), .opcode(Instrucao[15:13]), .MemToReg(CacheToReg), .Jump(Jump), .ALUOP(ALUOP),
    .stall(in_1));
  Banco_de_Registradores banco_de_registradores_1 (
    .WriteAddress(Instrucao[12:10]), .ReadAddress1(Instrucao[9:7]), .ReadAddress2(Instrucao[6:4]),
    .RegWrite(RegWrite), .Dados(Dado_t), .\Saída1 (\banco_de_registradores_1_saída1 ),
    .\Saída2 (\banco_de_registradores_1_saída2 ));
  assign bit_extender_2_out = {{6{1'b0}}, Desloc};  // Bit_Extender bit_extender_2
  Multiplexer #(.width(16), .enable("false")) multiplexer_1 (
    .in0(\banco_de_registradores_1_saída2 ), .in1(bit_extender_2_out), .out(multiplexer_1_out), .sel(AluSrc));
  ULA ula_1 (
    .Entrada1(\banco_de_registradores_1_saída1 ), .Entrada2(multiplexer_1_out),
    .Function(controleula_1_controle), .\Saída ({\ula_1_saída , readAddress}), .Igual(ula_1_igual));
  ControleULA controleula_1 (.Function(Instrucao[1:0]), .Controle(controleula_1_controle), .ALUOP(ALUOP));
  and and_1 (IsBranch_t, Branch, ula_1_igual);
  Multiplexer #(.width(16), .enable("false")) multiplexer_2 (
    .in0({\ula_1_saída , readAddress}), .in1(dado), .out(Dado_t), .sel(CacheToReg));
  Multiplexer #(.width(10), .enable("false")) multiplexer_3 (
    .in0(Desloc), .in1({10{1'b0}}), .out(Deslocamento), .sel(in_1));
  Multiplexer #(.enable("false")) multiplexer_4 (.in0(IsBranch_t), .in1(1'b0), .out(IsBranch), .sel(in_1));
  Multiplexer #(.width(10), .enable("false")) multiplexer_5 (
    .in0(Instrucao[12:3]), .in1({10{1'b0}}), .out(JumpAddress), .sel(in_1));
  Multiplexer #(.enable("false")) multiplexer_6 (.in0(CacheToReg), .in1(1'b0), .out(out_10), .sel(in_3));

  // Other names for the same wires on the sheet: JumpIMM[9:0] = Instrucao[12:3]; DadoCache[15:0] = dado;
  //   function[1:0] = Instrucao[1:0]; opcode[2:0] = Instrucao[15:13]; RD[2:0] = Instrucao[12:10];
  //   RS[2:0] = Instrucao[9:7]; RT[2:0] = Instrucao[6:4]; stall = in_1; turnOff = in_3
endmodule

module ULA (
  input  [15:0] Entrada1,
  input  [15:0] Entrada2,
  input  [1:0] Function,
  output [15:0] \Saída ,
  output Igual
);

  wire [15:0] AND, OR, Soma, \Subtração ;

  Adder #(.width(16)) adder_1 (.a(Entrada1), .b(Entrada2), .out(Soma));  // open: cin, cout
  Subtractor #(.width(16)) subtractor_1 (.a(Entrada1), .b(Entrada2), .out(\Subtração ));  // open: bin, bout
  assign AND = Entrada1 & Entrada2;  // AND_Gate and_1, 16 bits wide
  assign OR = Entrada1 | Entrada2;  // OR_Gate or_1, 16 bits wide
  Multiplexer #(.select(2), .width(16), .enable("false")) multiplexer_1 (
    .in0(Soma), .in1(\Subtração ), .in2(AND), .in3(OR), .out(\Saída ), .sel(Function));
  nor nor_1 (Igual, \Subtração [0], \Subtração [1], \Subtração [2], \Subtração [3], \Subtração [4], \Subtração [5], \Subtração [6], \Subtração [7], \Subtração [8], \Subtração [9], \Subtração [10], \Subtração [11], \Subtração [12], \Subtração [13], \Subtração [14], \Subtração [15]);
endmodule

module Banco_de_Registradores (
  input  [2:0] WriteAddress,
  input  [2:0] ReadAddress1,
  input  [2:0] ReadAddress2,
  input  RegWrite,
  input  [15:0] Dados,
  output [15:0] \Saída1 ,
  output [15:0] \Saída2 
);

  wire clock_1_out, write_r1, write_r2, write_r3, write_r4, write_r5, write_r6, write_r7;
  wire [15:0] r0, r1, r2, r3, r4, r5, r6, r7;

  Demultiplexer #(.select(3), .enable("false")) demultiplexer_1 (
    .out1(write_r1), .out2(write_r2), .out3(write_r3), .out4(write_r4), .out5(write_r5), .out6(write_r6),
    .out7(write_r7), .in(RegWrite), .sel(WriteAddress));  // open: out0
  Register #(.width(16)) register_1 (.D({16{1'b0}}), .Q(r0), .clk(clock_1_out));  // open: en, clr
  Register #(.width(16)) register_2 (.D(Dados), .en(write_r1), .Q(r1), .clk(clock_1_out));  // open: clr
  Register #(.width(16)) register_3 (.D(Dados), .en(write_r2), .Q(r2), .clk(clock_1_out));  // open: clr
  Register #(.width(16)) register_4 (.D(Dados), .en(write_r3), .Q(r3), .clk(clock_1_out));  // open: clr
  Register #(.width(16)) register_5 (.D(Dados), .en(write_r4), .Q(r4), .clk(clock_1_out));  // open: clr
  Register #(.width(16)) register_6 (.D(Dados), .en(write_r5), .Q(r5), .clk(clock_1_out));  // open: clr
  Register #(.width(16)) register_7 (.D(Dados), .en(write_r6), .Q(r6), .clk(clock_1_out));  // open: clr
  Register #(.width(16)) register_8 (.D(Dados), .en(write_r7), .Q(r7), .clk(clock_1_out));  // open: clr
  Clock clock_1 (.out(clock_1_out));
  Multiplexer #(.select(3), .width(16), .enable("false")) multiplexer_1 (
    .in0(r0), .in1(r1), .in2(r2), .in3(r3), .in4(r4), .in5(r5), .in6(r6), .in7(r7), .out(\Saída1 ),
    .sel(ReadAddress1));
  Multiplexer #(.select(3), .width(16), .enable("false")) multiplexer_2 (
    .in0(r0), .in1(r1), .in2(r2), .in3(r3), .in4(r4), .in5(r5), .in6(r6), .in7(r7), .out(\Saída2 ),
    .sel(ReadAddress2));

  // Other names for the same wires on the sheet: Dado[15:0] = Dados; saida1[15:0] = \Saída1 ; saida2[15:0] = \Saída2 
endmodule

// Unidade Controle
module Unidade_de_Controle (
  input  stall,
  input  [2:0] opcode,
  output RegDst,
  output RegWrite,
  output ALUSrc,
  output MemRead,
  output MemWrite,
  output Branch,
  output MemToReg,
  output Jump,
  output [2:0] ALUOP
);

  wire [10:0] multiplexer_1_out;

  Multiplexer #(.select(3), .width(11), .enable("false")) multiplexer_1 (
    .in0(11'h203), .in1(11'h4f), .in2(11'h14), .in3(11'h7), .in4(11'h307), .in5(11'h407), .in6(11'h20),
    .in7(11'h80), .out({multiplexer_1_out[10:7], MemToReg, multiplexer_1_out[5:0]}), .sel(opcode));
  Multiplexer #(.enable("false")) multiplexer_2 (.in0(multiplexer_1_out[0]), .in1(1'b0), .out(RegDst), .sel(stall));
  Multiplexer #(.enable("false")) multiplexer_3 (.in0(multiplexer_1_out[1]), .in1(1'b0), .out(RegWrite), .sel(stall));
  Multiplexer #(.enable("false")) multiplexer_4 (.in0(multiplexer_1_out[2]), .in1(1'b0), .out(ALUSrc), .sel(stall));
  Multiplexer #(.enable("false")) multiplexer_5 (.in0(multiplexer_1_out[3]), .in1(1'b0), .out(MemRead), .sel(stall));
  Multiplexer #(.enable("false")) multiplexer_6 (.in0(multiplexer_1_out[4]), .in1(1'b0), .out(MemWrite), .sel(stall));
  Multiplexer #(.enable("false")) multiplexer_7 (.in0(multiplexer_1_out[5]), .in1(1'b0), .out(Branch), .sel(stall));
  Multiplexer #(.enable("false")) multiplexer_8 (.in0(multiplexer_1_out[7]), .in1(1'b0), .out(Jump), .sel(stall));
  Multiplexer #(.width(3), .enable("false")) multiplexer_9 (
    .in0(multiplexer_1_out[10:8]), .in1(3'b000), .out(ALUOP), .sel(stall));
endmodule

module ControleULA (
  input  [1:0] Function,
  input  [2:0] ALUOP,
  output [1:0] Controle
);

  Multiplexer #(.select(3), .width(2), .enable("false")) multiplexer_1 (
    .in0(2'b00), .in1(2'b01), .in2(Function), .in3(2'b10), .in4(2'b11), .out(Controle), .sel(ALUOP));  // open: in5, in6, in7

  // Notes on the sheet:
  //   ADD
  //   SUB
  //   AND
  //   OR
endmodule
